# Fritzing sketch button_box_new version (saved by Fritzing 1.0.0rc)

parts:
  S1 = Toggle Switch spst [package=THT]
  S2 = Toggle Switch spst [package=THT]
  BT3 = Arcade Button (red)
  BT2 = Arcade Button (red)
  BT1 = Arcade Button (red)
  BT4 = Arcade Button (blue)
  BT5 = Arcade Button (blue)
  BT6 = Arcade Button (blue)
  LED1 = LED - 5mm [color="Red (633nm)" current=0.030 package="5 mm [THT]"]
  LE3 = LED - 5mm [color="Red (633nm)" current=0.030 package="5 mm [THT]"]
  LED2 = LED - 5mm [color="Red (633nm)" current=0.030 package="5 mm [THT]"]
  LED5 = LED - 5mm [color="Blue (525nm)" current=0.030 package="5 mm [THT]"]
  LED6 = LED - 5mm [color="Blue (525nm)" current=0.030 package="5 mm [THT]"]
  LED4 = LED - 5mm [color="Blue (525nm)" current=0.030 package="5 mm [THT]"]
  LED7 = LED - 5mm [color="Red (633nm)" part_number="internally connected" current=0.030 package="5 mm [THT]"]
  LED8 = LED - 5mm [color="Blue (525nm)" part_number=not_enough_gpio current=0.030 package="5 mm [THT]"]
  S3 = Toggle Switch spst [package=THT]
  Bauteil2 = 0.56" 7-segment LED Backpack [part_number=879]
  C1 = Capacitor Polarized [part_number=1000uF package=panasonic_e]
  JOY1 = Adafruit Arcade Joystick
  Bauteil3 = 16 NeoPixel Ring [part_number=1463]
  Part1 = Logic Level Converter
  Bauteil5 = Adafruit ESP32-S3 Feather [part_number="Adafruit #5323"]
  Bauteil6 = Pololu 5V Step-Up Regulator
  Bauteil7 = Adafruit MCP23017 STEMMA QT [part_number="Adafruit #5346"]
  BATT1 = LiPoly Battery (1300mAh)
  J1 = Piezo Speaker
  BT7 = Arcade Button (red)
  BT8 = Arcade Button (blue)
  LED9 = LED - 5mm [color="Blue (525nm)" current=0.030 package="5 mm [THT]"]
  LED10 = LED - 5mm [color="Red (633nm)" current=0.030 package="5 mm [THT]"]
  R1 = Resistor [tolerance=±5% power=0.25W resistance=350 package=THT]
  R2 = Resistor [tolerance=±5% power=0.25W resistance=220 package=THT]
  R3 = Resistor [tolerance=±5% power=0.25W resistance=220 package=THT]
  R4 = Resistor [tolerance=±5% power=0.25W resistance=220 package=THT]
  R5 = Resistor [tolerance=±5% power=0.25W resistance=220 package=THT]
  R6 = Resistor [tolerance=±5% power=0.25W resistance=220 package=THT]
  R7 = Resistor [tolerance=±5% power=0.25W resistance=220 package=THT]
  R8 = Resistor [tolerance=±5% power=0.25W resistance=220 package=THT]
  R9 = Resistor [tolerance=±5% power=0.25W resistance=220 package=THT]
  R10 = Resistor [tolerance=±5% resistance=220 package="1206 [SMD]"]
  R11 = Resistor [tolerance=±5% resistance=220 package="1206 [SMD]"]

nets:
  N1: S1.L1, LED8.anode, R10.Pin_1
  GND: S1.COM, S2.COM, BT3.no_name_yet#2, BT2.no_name_yet#2, BT1.no_name_yet#2, BT4.no_name_yet#2, BT5.no_name_yet#2, BT6.no_name_yet#2, LED1.cathode, LE3.cathode, LED2.cathode, LED5.cathode, LED6.cathode, LED4.cathode, LED7.cathode, LED8.cathode, Bauteil2.GND, C1.-, JOY1.COM, Bauteil3.GND, Part1.TX2_LV, Part1.RX2_LV, Part1.GND, Bauteil5.GND, Bauteil6.GND, Bauteil7.GND, BATT1.negative, J1.pin2, LED10.cathode, R1.Pin_1
  N2: S2.L1, LED7.anode
  N3: BT3.no_name_yet#1, Bauteil7.GPA2
  N4: BT2.no_name_yet#1, Bauteil7.GPA1
  N5: BT1.no_name_yet#1, Bauteil7.GPA0
  N6: BT4.no_name_yet#1, Bauteil7.GPA4
  N7: BT5.no_name_yet#1, Bauteil7.GPA5
  N8: BT6.no_name_yet#1, Bauteil7.GPA6
  N9: S3.L1, BATT1.positive
  N10: S3.COM, Bauteil5.VBAT, Bauteil6.VIN
  N11: Bauteil2.SCL, Bauteil5.SCL, Bauteil7.SCL
  N12: Bauteil2.SDA, Bauteil5.SDA, Bauteil7.SDA
  5V: Bauteil2.VDD, Bauteil5.VSENSOR, Bauteil7.VCC
  N13: C1.+, Bauteil3.VDD, Part1.TX_HV, Part1.RX_HV, Part1.HV, Bauteil6.VOUT
  N14: JOY1.N, Bauteil5.A0
  N15: JOY1.S, Bauteil5.A1
  N16: JOY1.W, Bauteil5.A2
  N17: JOY1.E, Bauteil5.A3
  N18: Bauteil3.IN, Part1.RX2_HV, Part1.TX2_HV
  N19: Part1.LV, Part1.RX_LV, Part1.TX_LV, Bauteil5.3.3V
  N20: Bauteil5.D10, R11.Pin_0
  N21: Bauteil5.D9, R10.Pin_0
  N22: Bauteil5.D6, R1.Pin_0
  N23: Bauteil7.GPA3, BT7.no_name_yet
  N24: Bauteil7.GPA7, BT8.no_name_yet#1
  N25: Bauteil7.GPB0, R5.Pin_0
  N26: Bauteil7.GPB1, R4.Pin_0
  N27: Bauteil7.GPB2, R3.Pin_0
  N28: Bauteil7.GPB3, R2.Pin_0
  N29: Bauteil7.GPB4, R6.Pin_0
  N30: Bauteil7.GPB5, R7.Pin_0
  N31: Bauteil7.GPB6, R8.Pin_0
  N32: Bauteil7.GPB7, R9.Pin_0
  N33: BT8.no_name_yet#2, LED9.cathode

notes:
  Arcade Stick - internal PullUp
  Arcade Buttons - Internal PullUp
  Vin|GND|Vout

custom parts:
  Toggle Switch spst: Toggle Switch single pole single throw
  Arcade Button (red): Adafruit Arcade Button (red)
  Arcade Button (blue): Adafruit Arcade Button (blue)
  0.56" 7-segment LED Backpack: This 0.56" 7-segment LED display includes a driver chip for simple control via an I2C interface. The backpack features address-selection jumpers so you can connect up to eight displays on a single I2C bus.
  16 NeoPixel Ring: 16 ultra bright smart LED NeoPixels are arranged in a circle with 1.75" (44.5mm) outer diameter. The rings are 'chainable' - connect the output pin of one to the input pin of another. Use only one microcontroller pin to control as many as you can chain together! Each LED is addressable as the driver chip is inside the LED. Each one has ~18mA constant current drive so the color will be very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
  Adafruit ESP32-S3 Feather: The ESP32-S3 has arrived in Feather format - and what a great way to get started with this powerful new chip from Espressif! With dual 240 MHz cores, WiFi and BLE support, and native USB, this Feather is great for powering your IoT projects. That's right - it's the new Adafruit ESP32-S3 Feather! With native USB and 8 MB flash, this board will let you upgrade your existing ESP32 projects.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
  Adafruit MCP23017 STEMMA QT: We’ve gotten a lot of requests for a MCP23017 breakout and we’ve always sorta been like “ehh why not just use the DIP chip?” but with STEMMA QT we could see the use case for a plug and play version that comes with all the passives on board. This Adafruit MCP23017 I2C GPIO Expander Breakout has 16 GPIO with matching ground pad. We particularly like the '17 as an expander for it's simple no-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
  LiPoly Battery (1300mAh): Lithium Ion Polymer Battery (1300mAh)
